# Fritzing sketch NRC_BBB (saved by Fritzing 0.9.2b)

parts:
  BeagleBone1 = BeagleBone Black
  U1 = 16-Channel Relay Module [package=relay-16ch]

nets:
  N1: BeagleBone1.no_name_yet#102, BeagleBone1.no_name_yet#104, U1.OUT_GND
  N2: BeagleBone1.no_name_yet#145, U1.IN16
  N3: BeagleBone1.no_name_yet#146, U1.IN15

custom parts:
  BeagleBone Black: BeagleBone Black rev. A5B
  16-Channel Relay Module: 16 channel relay module
